# Fritzing sketch MULTIWII_BOARD2 (saved by Fritzing 0.9.3b)
circuit board: 6cm x 6cm
breadboards: 1

parts:
  U1 = atmega328 [package=dip]
  RECEIVER = female pin header, 7 pins [form="♀ (female)"]
  XTAL1 = Crystal [frequency="16 MHz" package=THT]
  C1 = Ceramic Capacitor [capacitance=22pF package="100 mil [THT, multilayer]"]
  C2 = Ceramic Capacitor [capacitance=22pF package="100 mil [THT, multilayer]"]
  M1 = female pin header, 3 pins [form="♀ (female)"]
  M2 = female pin header, 3 pins [form="♀ (female)"]
  M3 = female pin header, 3 pins [form="♀ (female)"]
  M4 = female pin header, 3 pins [form="♀ (female)"]
  RESET = Pushbutton [package="[THT]"]
  R1 = Resistor [tolerance=±5% resistance=10k package=THT]
  BUZZER = female pin header, 2 pins [form="♀ (female)"]
  ISP = female pin header, 6 pins [form="♀ (female)"]
  VBAT = female pin header, 3 pins [form="♀ (female)"]
  C3 = Ceramic Capacitor [capacitance=100nF package="100 mil [THT, multilayer]"]
  C4 = Electrolytic Capacitor [capacitance=10µF package="100 mil [THT, electrolytic]"]
  GPS/FTDI = female pin header, 5 pins [form="♀ (female)"]
  C5 = Ceramic Capacitor [capacitance=100nF package="100 mil [THT, multilayer]"]
  Part2 = InvenSense MPU6050
  I2C = female pin header, 4 pins [form="♀ (female)"]

nets:
  reset: U1.RESET, RESET.Pin_1, RESET.Pin_2, R1.Pin_0, ISP.pin3, C5.0
  N1: U1.D0_(RX), GPS/FTDI.pin3
  N2: U1.D1_(TX), GPS/FTDI.pin4
  N3: U1.D2, RECEIVER.pin3
  N4: U1.D3_(PWM), M1.pin3
  N5: U1.D4, RECEIVER.pin4
  5V/avcc: U1.VCC, U1.AVCC, U1.AREF, R1.Pin_1, ISP.pin2, VBAT.pin2, C3.0, C4.+, GPS/FTDI.pin2, Part2.VCC, I2C.pin2
  GND: U1.GND, RECEIVER.pin1, C1.1, C2.1, M1.pin1, M2.pin1, M3.pin1, M4.pin1, RESET.Pin_3, RESET.Pin_4, BUZZER.pin1, ISP.pin1, C3.1, C4.-, GPS/FTDI.pin1, Part2.GND, I2C.pin1
  xlat1: U1.XLAT1, XTAL1.pin_1, C2.0
  xlat2: U1.XLAT2, XTAL1.pin_0, C1.0
  N6: U1.D5_(PWM), RECEIVER.pin5
  N7: U1.D6_(PWM), RECEIVER.pin6
  N8: U1.D7, RECEIVER.pin7
  N9: U1.D8, BUZZER.pin2
  N10: U1.D9_(PWM), M2.pin3
  N11: U1.D10_(PWM), M3.pin3
  mosi: U1.D11_(PWM), M4.pin3, ISP.pin6
  miso: U1.D12, ISP.pin5
  sck: U1.D13, ISP.pin4
  N12: U1.A3, VBAT.pin3
  sda: U1.A4, Part2.SDA, I2C.pin3
  scl: U1.A5, Part2.SCL, I2C.pin4
  N13: RECEIVER.pin2, M1.pin2, M2.pin2, M3.pin2, M4.pin2, VBAT.pin1
  N14: GPS/FTDI.pin5, C5.1

notes:
  PWR
  V

custom parts:
  InvenSense MPU6050: The InvenSense MPU-6050 sensor contains a MEMS accelerometer and a MEMS gyro in a single chip. It is very accurate, as it contains 16-bits analog to digital conversion hardware for each channel. Therefor it captures the x, y, and z channel at the same time. The sensor uses the I2C-bus to interface with the Arduino.
