# Fritzing sketch MULTIWII_VBAT (saved by Fritzing 0.9.3b)
circuit board: 3.6cm x 1.7cm
breadboards: 1

parts:
  R1 = Resistor [tolerance=±5% resistance=51k package=THT]
  R2 = Resistor [tolerance=±5% resistance=10k package=THT]
  R3 = Resistor [tolerance=±5% resistance=22k package=THT]
  VBAT = female pin header, 1 pin [form="♀ (female)"]
  R4 = Trimmer Potentiometer [maximum_resistance=5kΩ package=THT]
  BUZZER = Buzzer 12mm [package=buzzer-12mm-ns-kit]
  PWR = screw terminal, 2 pins
  BUZZER_2 = female pin header, 2 pins [form="♀ (female)"]

nets:
  N1: R1.Pin_0, R2.Pin_1, VBAT.pin1
  N2: R1.Pin_1, PWR.pin2
  N3: R2.Pin_0, R3.Pin_0
  N4: R3.Pin_1, R4.wiper
  GND: R4.leg1, BUZZER.2, PWR.pin1, BUZZER_2.pin1
  N5: BUZZER.1, BUZZER_2.pin2
