# Fritzing sketch power_distributor (saved by Fritzing 0.9.3b)
circuit board: 12.5cm x 2.5cm
breadboards: 1

parts:
  Pad1 = Pad [width=7.902222222222222 height=9.03111111111111 connect=center]
  Pad2 = Pad [width=7.902222222222222 height=9.03111111111111 connect=center]
  Pad3 = Pad [width=7.902222222222222 height=9.03111111111111 connect=center]
  Pad4 = Pad [width=7.902222222222222 height=9.03111111111111 connect=center]
  Pad5 = Pad [width=7.902222222222222 height=9.03111111111111 connect=center]
  Pad6 = Pad [width=7.902222222222222 height=9.03111111111111 connect=center]
  Pad7 = Pad [width=7.902222222222222 height=9.03111111111111 connect=center]
  Pad8 = Pad [width=7.902222222222222 height=9.03111111111111 connect=center]
  Pad9 = Pad [width=7.902222222222222 height=9.03111111111111 connect=center]
  Pad10 = Pad [width=7.902222222222222 height=9.03111111111111 connect=center]

nets:
  N1: Pad1.pad, Pad3.pad, Pad6.pad, Pad7.pad, Pad10.pad
  N2: Pad2.pad, Pad4.pad, Pad5.pad, Pad8.pad, Pad9.pad
